// Logisim project 4-bit binary up-down counter.circ as structural Verilog: 1 circuit, main circuit main
module main (
  input  UP,
  input  DOWN,
  input  Reset_Clear,
  output A0,
  output A1,
  output A2,
  output A3
);

  wire AND_2_out, AND_3_out, AND_4_out, AND_5_out, AND_6_out, AND_7_out, AND_out, CLK_out, d_ff_1_qn,
       d_ff_2_qn, d_ff_3_qn, not_1_out, OR_2_out, OR_3_out, OR_4_out, OR_out, XOR_2_out, XOR_3_out,
       XOR_4_out, XOR_out;

  not not_1 (not_1_out, UP);
  and AND (AND_out, not_1_out, DOWN);
  and AND_2 (AND_2_out, AND_out, d_ff_1_qn);
  and AND_3 (AND_3_out, AND_2_out, d_ff_2_qn);
  and AND_4 (AND_4_out, AND_3_out, d_ff_3_qn);
  and AND_5 (AND_5_out, UP, A0);
  and AND_6 (AND_6_out, AND_5_out, A1);
  and AND_7 (AND_7_out, AND_6_out, A2);
  or OR (OR_out, UP, AND_out);
  or OR_2 (OR_2_out, AND_5_out, AND_2_out);
  or OR_3 (OR_3_out, AND_6_out, AND_3_out);
  or OR_4 (OR_4_out, AND_7_out, AND_4_out);
  xor XOR (XOR_out, A0, OR_out);
  xor XOR_2 (XOR_2_out, A1, OR_2_out);
  xor XOR_3 (XOR_3_out, A2, OR_3_out);
  xor XOR_4 (XOR_4_out, A3, OR_4_out);
  Clock CLK (.out(CLK_out));
  D_Flip_Flop d_ff_1 (.clk(CLK_out), .D(XOR_out), .Q(A0), .Qn(d_ff_1_qn), .reset(Reset_Clear));  // open: preset, en
  D_Flip_Flop d_ff_2 (.clk(CLK_out), .D(XOR_2_out), .Q(A1), .Qn(d_ff_2_qn), .reset(Reset_Clear));  // open: preset, en
  D_Flip_Flop d_ff_3 (.clk(CLK_out), .D(XOR_3_out), .Q(A2), .Qn(d_ff_3_qn), .reset(Reset_Clear));  // open: preset, en
  D_Flip_Flop d_ff_4 (.clk(CLK_out), .D(XOR_4_out), .Q(A3), .reset(Reset_Clear));  // open: Qn, preset, en

  // Notes on the sheet:
  //   Circuit: 4-bit Binary Up-Down Counter
  //   Counting DOWN 2
endmodule
