// Logisim project 4-bit universal shift register.circ as structural Verilog: 1 circuit, main circuit main
module main (
  input  Clear,
  input  Enable,
  input  Preset,
  input  [1:0] S1__S0,
  input  Switch,
  input  Serial_Input_for_Shift_Right,
  input  Serial_Input_for_Shift_Left,
  input  I4,
  input  I3,
  input  I2,
  input  I1,
  output A4,
  output A3,
  output A2,
  output A1
);

  wire CLK_out, multiplexer_1_out, multiplexer_2_out, multiplexer_3_out, multiplexer_4_out;

  Clock CLK (.out(CLK_out));
  D_Flip_Flop d_ff_1 (
    .clk(CLK_out), .D(multiplexer_1_out), .Q(A4), .preset(Preset), .en(Enable), .reset(Clear));  // open: Qn
  Multiplexer #(.select(2)) multiplexer_1 (
    .in0(A4), .in1(Serial_Input_for_Shift_Right), .in2(A3), .in3(I4), .out(multiplexer_1_out), .sel(S1__S0),
    .en(Switch));
  D_Flip_Flop d_ff_2 (
    .clk(CLK_out), .D(multiplexer_2_out), .Q(A3), .preset(Preset), .en(Enable), .reset(Clear));  // open: Qn
  Multiplexer #(.select(2)) multiplexer_2 (
    .in0(A3), .in1(A4), .in2(A2), .in3(I3), .out(multiplexer_2_out), .sel(S1__S0), .en(Switch));
  D_Flip_Flop d_ff_3 (
    .clk(CLK_out), .D(multiplexer_3_out), .Q(A2), .preset(Preset), .en(Enable), .reset(Clear));  // open: Qn
  Multiplexer #(.select(2)) multiplexer_3 (
    .in0(A2), .in1(A3), .in2(A1), .in3(I2), .out(multiplexer_3_out), .sel(S1__S0), .en(Switch));
  D_Flip_Flop d_ff_4 (
    .clk(CLK_out), .D(multiplexer_4_out), .Q(A1), .preset(Preset), .en(Enable), .reset(Clear));  // open: Qn
  Multiplexer #(.select(2)) multiplexer_4 (
    .in0(A1), .in1(A2), .in2(Serial_Input_for_Shift_Left), .in3(I1), .out(multiplexer_4_out), .sel(S1__S0),
    .en(Switch));

  // Notes on the sheet:
  //   Shift Right
  //   Parallel Outputs
  //   --------------------------------------------------------------------------------------------------------
  //   Parallel Inputs
  //   4 Bit Universal Shift Register
  //   ------------------------------------------------------------------------------------------------
endmodule
