// Logisim project full adder circuit.circ as structural Verilog: 2 circuits, main circuit main
module main (
  input  Swtich,
  input  Cin,
  input  [1:0] S0__S1,
  input  A0,
  input  B0,
  input  _0,
  input  _1,
  input  A1,
  input  B1,
  input  _0_2,
  input  _1_2,
  output D0,
  output D1,
  output Cout
);

  wire FA_cout, multiplexer_1_out, multiplexer_2_out, not_1_out, not_2_out;

  not not_1 (not_1_out, B0);
  not not_2 (not_2_out, B1);
  Multiplexer #(.select(2)) multiplexer_1 (
    .in0(B0), .in1(not_1_out), .in2(_0), .in3(_1), .out(multiplexer_1_out), .sel(S0__S1), .en(Swtich));
  Multiplexer #(.select(2)) multiplexer_2 (
    .in0(B1), .in1(not_2_out), .in2(_0_2), .in3(_1_2), .out(multiplexer_2_out), .sel(S0__S1), .en(Swtich));
  Full_Adder_Circuit FA (.A(A0), .B(multiplexer_1_out), .S(D0), .Cin(Cin), .Cout(FA_cout));
  Full_Adder_Circuit FA_2 (.A(A1), .B(multiplexer_2_out), .S(D1), .Cin(FA_cout), .Cout(Cout));

  // Notes on the sheet:
  //   4x1 MUX
  //   4x1 MUX
  //   Design of A 2-bit Arithmetic Unit
  //   Microoperation: Add With Carry
endmodule

module Full_Adder_Circuit (
  input  Cin,
  input  A,
  input  B,
  output S,
  output Cout
);

  wire AND_2_out, AND_out, XOR_out;

  xor XOR (XOR_out, A, B);
  xor XOR_2 (S, XOR_out, Cin);
  and AND (AND_out, Cin, XOR_out);
  and AND_2 (AND_2_out, B, A);
  or OR (Cout, AND_out, AND_2_out);

  // Notes on the sheet:
  //   Full Adder Circuit
endmodule
